// Logisim project LAB2_2024-2.circ as structural Verilog: 8 circuits, main circuit register_bank_4
module register_bank_4 (
  input  [1:0] dir_A,
  input  [1:0] dir_B,
  input  [1:0] WRITE_address,
  input  [7:0] dato,
  input  clock_reg,
  input  reset_reg,
  output [7:0] ope_A,
  output [7:0] ope_B
);

  wire decoder_1_out0, decoder_1_out1, decoder_1_out2, decoder_1_out3;
  wire [3:0] binary_to_bcd_converter_1_p2, binary_to_bcd_converter_1_p3, binary_to_bcd_converter_1_p4,
       binary_to_bcd_converter_2_p2, binary_to_bcd_converter_2_p3, binary_to_bcd_converter_2_p4,
       binary_to_bcd_converter_3_p2, binary_to_bcd_converter_3_p3, binary_to_bcd_converter_3_p4,
       binary_to_bcd_converter_4_p2, binary_to_bcd_converter_4_p3, binary_to_bcd_converter_4_p4, R0_q,
       R0_q_2, R1_q, R1_q_2, R2_q, R2_q_2, R3_q, R3_q_2;

  Decoder #(.select(2)) decoder_1 (
    .out0(decoder_1_out0), .out1(decoder_1_out1), .out2(decoder_1_out2), .out3(decoder_1_out3),
    .sel(WRITE_address));  // open: en
  Register R3 (.D(dato), .en(decoder_1_out3), .clk(clock_reg), .Q({R3_q_2, R3_q}), .clr(reset_reg));
  Register R2 (.D(dato), .en(decoder_1_out2), .clk(clock_reg), .Q({R2_q_2, R2_q}), .clr(reset_reg));
  Register R1 (.D(dato), .en(decoder_1_out1), .clk(clock_reg), .Q({R1_q_2, R1_q}), .clr(reset_reg));
  Register R0 (.D(dato), .en(decoder_1_out0), .clk(clock_reg), .Q({R0_q_2, R0_q}), .clr(reset_reg));
  Hex_Digit_Display R3_hex_H (.value(R3_q_2));  // open: dp
  Hex_Digit_Display R2_hex_H (.value(R2_q_2));  // open: dp
  Hex_Digit_Display R1_hex_H (.value(R1_q_2));  // open: dp
  Hex_Digit_Display R0_hex_H (.value(R0_q_2));  // open: dp
  Hex_Digit_Display R3_hex_L (.value(R3_q));  // open: dp
  Hex_Digit_Display R2_hex_L (.value(R2_q));  // open: dp
  Hex_Digit_Display R1_hex_L (.value(R1_q));  // open: dp
  Hex_Digit_Display R0_hex_L (.value(R0_q));  // open: dp
  Hex_Digit_Display R3dec2 (.value(binary_to_bcd_converter_1_p2));  // open: dp
  // Binary_to_BCD_converter #(.binvalue(8)) binary_to_bcd_converter_1: pin names not known; wires that end beside it: {R3_q_2, R3_q}, binary_to_bcd_converter_1_p2, binary_to_bcd_converter_1_p3, binary_to_bcd_converter_1_p4
  Hex_Digit_Display R2dec2 (.value(binary_to_bcd_converter_2_p2));  // open: dp
  // Binary_to_BCD_converter #(.binvalue(8)) binary_to_bcd_converter_2: pin names not known; wires that end beside it: {R2_q_2, R2_q}, binary_to_bcd_converter_2_p2, binary_to_bcd_converter_2_p3, binary_to_bcd_converter_2_p4
  Hex_Digit_Display R1dec2 (.value(binary_to_bcd_converter_3_p2));  // open: dp
  // Binary_to_BCD_converter #(.binvalue(8)) binary_to_bcd_converter_3: pin names not known; wires that end beside it: {R1_q_2, R1_q}, binary_to_bcd_converter_3_p2, binary_to_bcd_converter_3_p3, binary_to_bcd_converter_3_p4
  Hex_Digit_Display R0dec2 (.value(binary_to_bcd_converter_4_p2));  // open: dp
  // Binary_to_BCD_converter #(.binvalue(8)) binary_to_bcd_converter_4: pin names not known; wires that end beside it: {R0_q_2, R0_q}, binary_to_bcd_converter_4_p2, binary_to_bcd_converter_4_p3, binary_to_bcd_converter_4_p4
  Hex_Digit_Display R3dec1 (.value(binary_to_bcd_converter_1_p3));  // open: dp
  Hex_Digit_Display R3dec0 (.value(binary_to_bcd_converter_1_p4));  // open: dp
  Hex_Digit_Display R2dec1 (.value(binary_to_bcd_converter_2_p3));  // open: dp
  Hex_Digit_Display R2dec0 (.value(binary_to_bcd_converter_2_p4));  // open: dp
  Hex_Digit_Display R1dec1 (.value(binary_to_bcd_converter_3_p3));  // open: dp
  Hex_Digit_Display R1dec0 (.value(binary_to_bcd_converter_3_p4));  // open: dp
  Hex_Digit_Display R0dec1 (.value(binary_to_bcd_converter_4_p3));  // open: dp
  Hex_Digit_Display R0dec0 (.value(binary_to_bcd_converter_4_p4));  // open: dp
  Multiplexer #(.select(2), .width(8)) multiplexer_1 (
    .in0({R0_q_2, R0_q}), .in1({R1_q_2, R1_q}), .in2({R2_q_2, R2_q}), .in3({R3_q_2, R3_q}), .out(ope_A),
    .sel(dir_A));
  Multiplexer #(.select(2), .width(8)) multiplexer_2 (
    .in0({R0_q_2, R0_q}), .in1({R1_q_2, R1_q}), .in2({R2_q_2, R2_q}), .in3({R3_q_2, R3_q}), .out(ope_B),
    .sel(dir_B));
endmodule

module preg1 (
);

  wire clock_1_out, clock_2_out, reset;
  wire [1:0] dir_A, dir_b, dir_RES, operation;
  wire [4:0] progcounter_32_1_pc;
  wire [7:0] adder_1_out, and_1_out, multiplexer_1_out, not_1_out, or_1_out, register_bank_4_1_ope_a,
       register_bank_4_1_ope_b;

  ROM #(.addrWidth(5)) rom_1 (.addr(progcounter_32_1_pc), .data({dir_RES, dir_A, operation, dir_b}));
  ProgCounter_32 progcounter_32_1 (.reset_PC(reset), .clock_PC(clock_1_out), .PC(progcounter_32_1_pc));
  Clock clock_1 (.out(clock_1_out));
  Button button_1 (.out(reset));
  Clock clock_2 (.out(clock_2_out));
  Multiplexer #(.select(2), .width(8)) multiplexer_1 (
    .in0(not_1_out), .in1(and_1_out), .in2(or_1_out), .in3(adder_1_out), .out(multiplexer_1_out),
    .sel(operation));
  register_bank_4 register_bank_4_1 (
    .WRITE_address(dir_RES), .clock_reg(clock_2_out), .reset_reg(reset), .dato(multiplexer_1_out),
    .dir_A(dir_A), .dir_B(dir_b), .ope_A(register_bank_4_1_ope_a), .ope_B(register_bank_4_1_ope_b));
  assign not_1_out = ~register_bank_4_1_ope_b;  // NOT_Gate not_1, 8 bits wide
  assign and_1_out = register_bank_4_1_ope_b & register_bank_4_1_ope_a;  // AND_Gate and_1, 8 bits wide
  assign or_1_out = register_bank_4_1_ope_b | register_bank_4_1_ope_a;  // OR_Gate or_1, 8 bits wide
  Adder adder_1 (.a(register_bank_4_1_ope_a), .b(register_bank_4_1_ope_b), .out(adder_1_out));  // open: cin, cout

  // Notes on the sheet:
  //   contents of rom_1 (hex, n*v repeats v):
  //   0 c 0 cc 8b 7e 1f
endmodule

module ProgCounter_16 (
  input  reset_PC,
  input  clock_PC,
  output [3:0] PC
);

  Counter #(.max('hf), .width(4)) counter_1 (
    .clr(reset_PC), .load(1'b0), .up(1'b1), .count(1'b1), .clk(clock_PC), .Q(PC));  // open: D, carry
  Hex_Digit_Display hex_digit_display_1 (.value(PC));  // open: dp
endmodule

module ProgCounter_32 (
  input  reset_PC,
  input  clock_PC,
  output [4:0] PC
);

  wire [3:0] binary_to_bcd_converter_1_p2, binary_to_bcd_converter_1_p3;

  Counter #(.max('h1f), .width(5)) counter_1 (
    .clr(reset_PC), .load(1'b0), .up(1'b1), .count(1'b1), .clk(clock_PC), .Q(PC));  // open: D, carry
  Hex_Digit_Display hex1 (.value({3'b000, PC[4]}));  // open: dp
  Hex_Digit_Display hex0 (.value(PC[3:0]));  // open: dp
  Hex_Digit_Display dec1 (.value(binary_to_bcd_converter_1_p2));  // open: dp
  // Binary_to_BCD_converter #(.binvalue(5)) binary_to_bcd_converter_1: pin names not known; wires that end beside it: PC, binary_to_bcd_converter_1_p2, binary_to_bcd_converter_1_p3
  Hex_Digit_Display dec0 (.value(binary_to_bcd_converter_1_p3));  // open: dp
endmodule

module preg2 (
);

  wire clock_1_out, clock_2_out, reset;
  wire [1:0] dirB;
  wire [2:0] dirA, Op;
  wire [4:0] progcounter_32_1_pc;
  wire [7:0] adder_1_out, and_1_out, lsl_1_out_2, lsr_1_out_2, multiplexer_1_out, not_1_out, opeB, or_1_out,
       register_bank_8_1_ope_a;

  ProgCounter_32 progcounter_32_1 (.reset_PC(reset), .clock_PC(clock_2_out), .PC(progcounter_32_1_pc));
  ROM #(.addrWidth(5)) rom_1 (.addr(progcounter_32_1_pc), .data({Op, dirA, dirB}));
  Clock clock_1 (.out(clock_1_out));
  Clock clock_2 (.out(clock_2_out));
  register_bank_8 register_bank_8_1 (
    .clock_reg(clock_1_out), .reset_reg(reset), .dir_DATO(dirA), .dato(multiplexer_1_out), .dir_A(dirA),
    .dir_B(dirB), .ope_A(register_bank_8_1_ope_a), .ope_B(opeB));
  assign not_1_out = ~register_bank_8_1_ope_a;  // NOT_Gate not_1, 8 bits wide
  assign and_1_out = register_bank_8_1_ope_a & opeB;  // AND_Gate and_1, 8 bits wide
  assign or_1_out = register_bank_8_1_ope_a | opeB;  // OR_Gate or_1, 8 bits wide
  Adder adder_1 (.a(register_bank_8_1_ope_a), .b(opeB), .out(adder_1_out));  // open: cin, cout
  LSL lsl_1 (.in_1(register_bank_8_1_ope_a), .out_2(lsl_1_out_2));
  LSR lsr_1 (.in_1(register_bank_8_1_ope_a), .out_2(lsr_1_out_2));
  Button button_1 (.out(reset));
  Multiplexer #(.select(3), .width(8)) multiplexer_1 (
    .in0(and_1_out), .in1(or_1_out), .in2(adder_1_out), .in3(opeB), .in4(not_1_out), .in5(lsl_1_out_2),
    .in6(lsr_1_out_2), .in7({{6{1'b0}}, dirB}), .out(multiplexer_1_out), .sel(Op));
endmodule

module register_bank_8 (
  input  [2:0] dir_DATO,
  input  [2:0] dir_A,
  input  [1:0] dir_B,
  input  [7:0] dato,
  input  clock_reg,
  input  reset_reg,
  output [7:0] ope_A,
  output [7:0] ope_B
);

  wire decoder_1_out0, decoder_1_out1, decoder_1_out2, decoder_1_out3, decoder_1_out4, decoder_1_out5,
       decoder_1_out6, decoder_1_out7;
  wire [3:0] binary_to_bcd_converter_1_p2, binary_to_bcd_converter_1_p3, binary_to_bcd_converter_1_p4,
       binary_to_bcd_converter_2_p2, binary_to_bcd_converter_2_p3, binary_to_bcd_converter_2_p4,
       binary_to_bcd_converter_3_p2, binary_to_bcd_converter_3_p3, binary_to_bcd_converter_3_p4,
       binary_to_bcd_converter_4_p2, binary_to_bcd_converter_4_p3, binary_to_bcd_converter_4_p4,
       binary_to_bcd_converter_5_p2, binary_to_bcd_converter_5_p3, binary_to_bcd_converter_5_p4,
       binary_to_bcd_converter_6_p2, binary_to_bcd_converter_6_p3, binary_to_bcd_converter_6_p4,
       binary_to_bcd_converter_7_p2, binary_to_bcd_converter_7_p3, binary_to_bcd_converter_7_p4,
       binary_to_bcd_converter_8_p2, binary_to_bcd_converter_8_p3, binary_to_bcd_converter_8_p4, R0_q,
       R0_q_2, R1_q, R1_q_2, R2_q, R2_q_2, R3_q, R3_q_2, register_1_q, register_1_q_2, register_2_q,
       register_2_q_2, register_3_q, register_3_q_2, register_4_q, register_4_q_2;

  Decoder #(.select(3)) decoder_1 (
    .out0(decoder_1_out0), .out1(decoder_1_out1), .out2(decoder_1_out2), .out3(decoder_1_out3),
    .out4(decoder_1_out4), .out5(decoder_1_out5), .out6(decoder_1_out6), .out7(decoder_1_out7), .sel(dir_DATO));  // open: en
  Register register_1 (
    .D(dato), .en(decoder_1_out7), .clk(clock_reg), .Q({register_1_q_2, register_1_q}), .clr(reset_reg));
  Register register_2 (
    .D(dato), .en(decoder_1_out6), .clk(clock_reg), .Q({register_2_q_2, register_2_q}), .clr(reset_reg));
  Register register_3 (
    .D(dato), .en(decoder_1_out5), .clk(clock_reg), .Q({register_3_q_2, register_3_q}), .clr(reset_reg));
  Register register_4 (
    .D(dato), .en(decoder_1_out4), .clk(clock_reg), .Q({register_4_q_2, register_4_q}), .clr(reset_reg));
  Register R3 (.D(dato), .en(decoder_1_out3), .clk(clock_reg), .Q({R3_q_2, R3_q}), .clr(reset_reg));
  Register R2 (.D(dato), .en(decoder_1_out2), .clk(clock_reg), .Q({R2_q_2, R2_q}), .clr(reset_reg));
  Register R1 (.D(dato), .en(decoder_1_out1), .clk(clock_reg), .Q({R1_q_2, R1_q}), .clr(reset_reg));
  Register R0 (.D(dato), .en(decoder_1_out0), .clk(clock_reg), .Q({R0_q_2, R0_q}), .clr(reset_reg));
  Hex_Digit_Display R7_h_H (.value(register_1_q_2));  // open: dp
  Hex_Digit_Display R6_h_H (.value(register_2_q_2));  // open: dp
  Hex_Digit_Display R5_h_H (.value(register_3_q_2));  // open: dp
  Hex_Digit_Display R4_h_H (.value(register_4_q_2));  // open: dp
  Hex_Digit_Display R3_hex_H (.value(R3_q_2));  // open: dp
  Hex_Digit_Display R2_hex_H (.value(R2_q_2));  // open: dp
  Hex_Digit_Display R1_hex_H (.value(R1_q_2));  // open: dp
  Hex_Digit_Display R0_hex_H (.value(R0_q_2));  // open: dp
  Hex_Digit_Display R7_h_L (.value(register_1_q));  // open: dp
  Hex_Digit_Display R6_h_L (.value(register_2_q));  // open: dp
  Hex_Digit_Display R5_h_L (.value(register_3_q));  // open: dp
  Hex_Digit_Display R4_h_L (.value(register_4_q));  // open: dp
  Hex_Digit_Display R3_hex_L (.value(R3_q));  // open: dp
  Hex_Digit_Display R2_hex_L (.value(R2_q));  // open: dp
  Hex_Digit_Display R1_hex_L (.value(R1_q));  // open: dp
  Hex_Digit_Display R0_hex_L (.value(R0_q));  // open: dp
  Hex_Digit_Display R7d2 (.value(binary_to_bcd_converter_1_p2));  // open: dp
  // Binary_to_BCD_converter #(.binvalue(8)) binary_to_bcd_converter_1: pin names not known; wires that end beside it: {register_1_q_2, register_1_q}, binary_to_bcd_converter_1_p2, binary_to_bcd_converter_1_p3, binary_to_bcd_converter_1_p4
  Hex_Digit_Display R6d2 (.value(binary_to_bcd_converter_2_p2));  // open: dp
  // Binary_to_BCD_converter #(.binvalue(8)) binary_to_bcd_converter_2: pin names not known; wires that end beside it: {register_2_q_2, register_2_q}, binary_to_bcd_converter_2_p2, binary_to_bcd_converter_2_p3, binary_to_bcd_converter_2_p4
  Hex_Digit_Display R5d2 (.value(binary_to_bcd_converter_3_p2));  // open: dp
  // Binary_to_BCD_converter #(.binvalue(8)) binary_to_bcd_converter_3: pin names not known; wires that end beside it: {register_3_q_2, register_3_q}, binary_to_bcd_converter_3_p2, binary_to_bcd_converter_3_p3, binary_to_bcd_converter_3_p4
  Hex_Digit_Display R4d2 (.value(binary_to_bcd_converter_4_p2));  // open: dp
  // Binary_to_BCD_converter #(.binvalue(8)) binary_to_bcd_converter_4: pin names not known; wires that end beside it: {register_4_q_2, register_4_q}, binary_to_bcd_converter_4_p2, binary_to_bcd_converter_4_p3, binary_to_bcd_converter_4_p4
  Hex_Digit_Display R3dec2 (.value(binary_to_bcd_converter_5_p2));  // open: dp
  // Binary_to_BCD_converter #(.binvalue(8)) binary_to_bcd_converter_5: pin names not known; wires that end beside it: {R3_q_2, R3_q}, binary_to_bcd_converter_5_p2, binary_to_bcd_converter_5_p3, binary_to_bcd_converter_5_p4
  Hex_Digit_Display R2dec2 (.value(binary_to_bcd_converter_6_p2));  // open: dp
  // Binary_to_BCD_converter #(.binvalue(8)) binary_to_bcd_converter_6: pin names not known; wires that end beside it: {R2_q_2, R2_q}, binary_to_bcd_converter_6_p2, binary_to_bcd_converter_6_p3, binary_to_bcd_converter_6_p4
  Hex_Digit_Display R1dec2 (.value(binary_to_bcd_converter_7_p2));  // open: dp
  // Binary_to_BCD_converter #(.binvalue(8)) binary_to_bcd_converter_7: pin names not known; wires that end beside it: {R1_q_2, R1_q}, binary_to_bcd_converter_7_p2, binary_to_bcd_converter_7_p3, binary_to_bcd_converter_7_p4
  Hex_Digit_Display R0dec2 (.value(binary_to_bcd_converter_8_p2));  // open: dp
  // Binary_to_BCD_converter #(.binvalue(8)) binary_to_bcd_converter_8: pin names not known; wires that end beside it: {R0_q_2, R0_q}, binary_to_bcd_converter_8_p2, binary_to_bcd_converter_8_p3, binary_to_bcd_converter_8_p4
  Hex_Digit_Display R7d1 (.value(binary_to_bcd_converter_1_p3));  // open: dp
  Hex_Digit_Display R7d0 (.value(binary_to_bcd_converter_1_p4));  // open: dp
  Hex_Digit_Display R6d1 (.value(binary_to_bcd_converter_2_p3));  // open: dp
  Hex_Digit_Display R6d0 (.value(binary_to_bcd_converter_2_p4));  // open: dp
  Hex_Digit_Display R5d1 (.value(binary_to_bcd_converter_3_p3));  // open: dp
  Hex_Digit_Display R5d0 (.value(binary_to_bcd_converter_3_p4));  // open: dp
  Hex_Digit_Display R4d1 (.value(binary_to_bcd_converter_4_p3));  // open: dp
  Hex_Digit_Display R4d0 (.value(binary_to_bcd_converter_4_p4));  // open: dp
  Hex_Digit_Display R3dec1 (.value(binary_to_bcd_converter_5_p3));  // open: dp
  Hex_Digit_Display R3dec0 (.value(binary_to_bcd_converter_5_p4));  // open: dp
  Hex_Digit_Display R2dec1 (.value(binary_to_bcd_converter_6_p3));  // open: dp
  Hex_Digit_Display R2dec0 (.value(binary_to_bcd_converter_6_p4));  // open: dp
  Hex_Digit_Display R1dec1 (.value(binary_to_bcd_converter_7_p3));  // open: dp
  Hex_Digit_Display R1dec0 (.value(binary_to_bcd_converter_7_p4));  // open: dp
  Hex_Digit_Display R0dec1 (.value(binary_to_bcd_converter_8_p3));  // open: dp
  Hex_Digit_Display R0dec0 (.value(binary_to_bcd_converter_8_p4));  // open: dp
  Multiplexer #(.select(3), .width(8)) multiplexer_1 (
    .in0({R0_q_2, R0_q}), .in1({R1_q_2, R1_q}), .in2({R2_q_2, R2_q}), .in3({R3_q_2, R3_q}),
    .in4({register_4_q_2, register_4_q}), .in5({register_3_q_2, register_3_q}),
    .in6({register_2_q_2, register_2_q}), .in7({register_1_q_2, register_1_q}), .out(ope_A), .sel(dir_A));
  Multiplexer #(.select(2), .width(8)) multiplexer_2 (
    .in0({R0_q_2, R0_q}), .in1({R1_q_2, R1_q}), .in2({R2_q_2, R2_q}), .in3({R3_q_2, R3_q}), .out(ope_B),
    .sel(dir_B));
endmodule

module LSL (
  input  [7:0] in_1,
  output [7:0] out_2
);


  assign out_2 = {in_1[6:0], 1'b0};
endmodule

module LSR (
  input  [7:0] in_1,
  output [7:0] out_2
);


  assign out_2 = {1'b0, in_1[7:1]};
endmodule
