// Logisim project AC_Lab2_25_1_yoshi.circ as structural Verilog
module main (
);

  wire button_1_out, clock_1_out;
  wire [1:0] dirA, dirB, dirW;
  wire [2:0] counter_1_q;
  wire [3:0] adder_2_out, divider_1_out, multiplier_1_out, subtractor_1_out;
  wire [7:0] A, adder_1_out, B, multiplexer_1_out, xnor_1_out;
  wire [7:6] entrada;

  Counter #(.max('h5), .width(3)) counter_1 (
    .clr(button_1_out), .clk(clock_1_out), .Q(counter_1_q));  // open: load, up, count, D, carry
  registers_2 registers_2_1 (
    .dir_RA(dirA), .dir_RB(dirB), .reset(button_1_out), .clock(clock_1_out), .dato_W(multiplexer_1_out),
    .dir_W(dirW), .RA(A), .RB(B));
  Button button_1 (.out(button_1_out));
  Clock clock_1 (.out(clock_1_out));
  ROM #(.addrWidth(3)) rom_1 (.addr(counter_1_q), .data({entrada, dirW, dirA, dirB}));
  Adder adder_1 (.a(A), .b(B), .out(adder_1_out));  // open: cin, cout
  Multiplier #(.width(4)) multiplier_1 (.a(A[7:4]), .b(4'b0101), .out(multiplier_1_out));  // open: cin, cout
  assign xnor_1_out = ~(A ^ B);  // XNOR_Gate xnor_1, 8 bits wide
  Divider #(.width(4)) divider_1 (.a(A[3:0]), .b(adder_2_out), .out(divider_1_out));  // open: upper, rem
  Subtractor #(.width(4)) subtractor_1 (.a(multiplier_1_out), .b(B[7:4]), .out(subtractor_1_out));  // open: bin, bout
  Adder #(.width(4)) adder_2 (.a(B[3:0]), .b(4'b0100), .out(adder_2_out));  // open: cin, cout
  Multiplexer #(.select(2), .width(8)) multiplexer_1 (
    .in0(adder_1_out), .in1({B[7:5], A[4:0]}), .in2({subtractor_1_out, divider_1_out}), .in3(xnor_1_out),
    .out(multiplexer_1_out), .sel(entrada));

  // Other names for the same wires on the sheet: entrada[5:0] = {dirW, dirA, dirB}; ope[1:0] = entrada

  // Notes on the sheet:
  //   C0-30-33-A3-CE-51
  //   contents of rom_1 (hex, n*v repeats v):
  //   c0 30 33 a3 ce 51
  //   Aquí puede hacer pruebas, pero no coloque aquí su diseño final
endmodule

module registers_2 (
  input  reset,
  input  clock,
  input  [7:0] dato_W,
  input  [1:0] dir_W,
  input  [1:0] dir_RA,
  input  [1:0] dir_RB,
  output [7:0] RA,
  output [7:0] RB
);

  wire decoder_1_out0, decoder_1_out1, decoder_1_out2, decoder_1_out3;
  wire [7:0] R0_q, R1_q, R2_q, R3_q;

  Decoder #(.select(2)) decoder_1 (
    .out0(decoder_1_out0), .out1(decoder_1_out1), .out2(decoder_1_out2), .out3(decoder_1_out3), .sel(dir_W));  // open: en
  Register R3 (.D(dato_W), .en(decoder_1_out3), .clk(clock), .Q(R3_q), .clr(reset));
  Register R2 (.D(dato_W), .en(decoder_1_out2), .clk(clock), .Q(R2_q), .clr(reset));
  Register R1 (.D(dato_W), .en(decoder_1_out1), .clk(clock), .Q(R1_q), .clr(reset));
  Register R0 (.D(dato_W), .en(decoder_1_out0), .clk(clock), .Q(R0_q), .clr(reset));
  Hex_Digit_Display R3H (.value(R3_q[7:4]));  // open: dp
  Hex_Digit_Display R2H (.value(R2_q[7:4]));  // open: dp
  Hex_Digit_Display R1H (.value(R1_q[7:4]));  // open: dp
  Hex_Digit_Display R0H (.value(R0_q[7:4]));  // open: dp
  Hex_Digit_Display R3L (.value(R3_q[3:0]));  // open: dp
  Hex_Digit_Display R2L (.value(R2_q[3:0]));  // open: dp
  Hex_Digit_Display R1L (.value(R1_q[3:0]));  // open: dp
  Hex_Digit_Display R0L (.value(R0_q[3:0]));  // open: dp
  Multiplexer #(.select(2), .width(8)) multiplexer_1 (
    .in0(R0_q), .in1(R1_q), .in2(R2_q), .in3(R3_q), .out(RA), .sel(dir_RA));
  Multiplexer #(.select(2), .width(8)) multiplexer_2 (
    .in0(R0_q), .in1(R1_q), .in2(R2_q), .in3(R3_q), .out(RB), .sel(dir_RB));
endmodule
