// Logisim project LAB_2.circ as structural Verilog
module main (
  output [7:0] out_1,
  output [7:0] out_2,
  output [7:0] out_3
);

  wire button_1_out, clock_1_out;
  wire [1:0] dirA, dirB, dirW, ope;
  wire [2:0] counter_1_q;
  wire [7:0] adder_1_out, bitrage_2_1_out_3, nibble_2_1_out_3, xnor_1_out;

  Clock clock_1 (.out(clock_1_out));
  Button button_1 (.out(button_1_out));
  Counter #(.max('h7), .width(3)) counter_1 (
    .clr(button_1_out), .clk(clock_1_out), .Q(counter_1_q));  // open: load, up, count, D, carry
  ROM #(.addrWidth(3)) rom_1 (.addr(counter_1_q), .data({ope, dirW, dirA, dirB}));
  registers_2 registers_2_1 (
    .dir_RA(dirA), .dir_RB(dirB), .reset(button_1_out), .clock(clock_1_out), .dato_W(out_3), .dir_W(dirW),
    .RA(out_1), .RB(out_2));
  Adder adder_1 (.a(out_1), .b(out_2), .out(adder_1_out));  // open: cin, cout
  nibble_2 nibble_2_1 (.RA(out_1), .RB(out_2), .out_3(nibble_2_1_out_3));
  assign xnor_1_out = ~(out_1 ^ out_2);  // XNOR_Gate xnor_1, 8 bits wide
  bitrage_2 bitrage_2_1 (.RA(out_1), .RB(out_2), .out_3(bitrage_2_1_out_3));
  Multiplexer #(.select(2), .width(8)) multiplexer_1 (
    .in0(adder_1_out), .in1(bitrage_2_1_out_3), .in2(nibble_2_1_out_3), .in3(xnor_1_out), .out(out_3),
    .sel(ope));

  // Notes on the sheet:
  //   contents of rom_1 (hex, n*v repeats v):
  //   c0 94 14 14 14
  //   Aquí puede hacer pruebas, pero no coloque aquí su diseño final
endmodule

module registers_2 (
  input  reset,
  input  clock,
  input  [7:0] dato_W,
  input  [1:0] dir_W,
  input  [1:0] dir_RA,
  input  [1:0] dir_RB,
  output [7:0] RA,
  output [7:0] RB
);

  wire decoder_1_out0, decoder_1_out1, decoder_1_out2, decoder_1_out3;
  wire [7:0] R0_q, R1_q, R2_q, R3_q;

  Decoder #(.select(2)) decoder_1 (
    .out0(decoder_1_out0), .out1(decoder_1_out1), .out2(decoder_1_out2), .out3(decoder_1_out3), .sel(dir_W));  // open: en
  Register R3 (.D(dato_W), .en(decoder_1_out3), .clk(clock), .Q(R3_q), .clr(reset));
  Register R2 (.D(dato_W), .en(decoder_1_out2), .clk(clock), .Q(R2_q), .clr(reset));
  Register R1 (.D(dato_W), .en(decoder_1_out1), .clk(clock), .Q(R1_q), .clr(reset));
  Register R0 (.D(dato_W), .en(decoder_1_out0), .clk(clock), .Q(R0_q), .clr(reset));
  Hex_Digit_Display R3H (.value(R3_q[7:4]));  // open: dp
  Hex_Digit_Display R2H (.value(R2_q[7:4]));  // open: dp
  Hex_Digit_Display R1H (.value(R1_q[7:4]));  // open: dp
  Hex_Digit_Display R0H (.value(R0_q[7:4]));  // open: dp
  Hex_Digit_Display R3L (.value(R3_q[3:0]));  // open: dp
  Hex_Digit_Display R2L (.value(R2_q[3:0]));  // open: dp
  Hex_Digit_Display R1L (.value(R1_q[3:0]));  // open: dp
  Hex_Digit_Display R0L (.value(R0_q[3:0]));  // open: dp
  Multiplexer #(.select(2), .width(8)) multiplexer_1 (
    .in0(R0_q), .in1(R1_q), .in2(R2_q), .in3(R3_q), .out(RA), .sel(dir_RA));
  Multiplexer #(.select(2), .width(8)) multiplexer_2 (
    .in0(R0_q), .in1(R1_q), .in2(R2_q), .in3(R3_q), .out(RB), .sel(dir_RB));
endmodule

module nibble_2 (
  input  [7:0] RA,
  input  [7:0] RB,
  output [7:0] out_3
);

  wire [3:0] adder_1_out, multiplier_1_out;

  Adder #(.width(4)) adder_1 (.a(RB[3:0]), .b(4'b0100), .out(adder_1_out));  // open: cin, cout
  Multiplier #(.width(4)) multiplier_1 (.a(RA[7:4]), .b(4'b0101), .out(multiplier_1_out));  // open: cin, cout
  Subtractor #(.width(4)) subtractor_1 (.a(multiplier_1_out), .b(RB[7:4]), .out(out_3[7:4]));  // open: bin, bout
  Divider #(.width(4)) divider_1 (.a(RA[3:0]), .b(adder_1_out), .out(out_3[3:0]));  // open: upper, rem

  // Notes on the sheet:
  //   BN1
  //   AN1
  //   BN0
  //   AN0
  //   RW1
  //   RW0
endmodule

module bitrage_2 (
  input  [7:0] RA,
  input  [7:0] RB,
  output [7:0] out_3
);


  assign out_3 = {RB[7:5], RA[4:0]};
endmodule
