// Logisim project Plantilla.circ as structural Verilog
module main (
  input  [1:0] in_1,
  input  [1:0] in_2,
  input  [1:0] in_3,
  input  [7:0] in_4,
  output [7:0] out_5,
  output [7:0] out_6
);

  wire button_1_out, clock_1_out;

  Clock clock_1 (.out(clock_1_out));
  registers_2 registers_2_1 (
    .dir_RA(in_1), .dir_RB(in_2), .reset(button_1_out), .clock(clock_1_out), .dato_W(in_4), .dir_W(in_3),
    .RA(out_5), .RB(out_6));
  Button button_1 (.out(button_1_out));

  // Notes on the sheet:
  //   Aquí puede hacer pruebas, pero no coloque aquí su diseño final
endmodule

module registers_2 (
  input  reset,
  input  clock,
  input  [7:0] dato_W,
  input  [1:0] dir_W,
  input  [1:0] dir_RA,
  input  [1:0] dir_RB,
  output [7:0] RA,
  output [7:0] RB
);

  wire decoder_1_out0, decoder_1_out1, decoder_1_out2, decoder_1_out3;
  wire [7:0] R0_q, R1_q, R2_q, R3_q;

  Decoder #(.select(2)) decoder_1 (
    .out0(decoder_1_out0), .out1(decoder_1_out1), .out2(decoder_1_out2), .out3(decoder_1_out3), .sel(dir_W));  // open: en
  Register R3 (.D(dato_W), .en(decoder_1_out3), .clk(clock), .Q(R3_q), .clr(reset));
  Register R2 (.D(dato_W), .en(decoder_1_out2), .clk(clock), .Q(R2_q), .clr(reset));
  Register R1 (.D(dato_W), .en(decoder_1_out1), .clk(clock), .Q(R1_q), .clr(reset));
  Register R0 (.D(dato_W), .en(decoder_1_out0), .clk(clock), .Q(R0_q), .clr(reset));
  Hex_Digit_Display R3H (.value(R3_q[7:4]));  // open: dp
  Hex_Digit_Display R2H (.value(R2_q[7:4]));  // open: dp
  Hex_Digit_Display R1H (.value(R1_q[7:4]));  // open: dp
  Hex_Digit_Display R0H (.value(R0_q[7:4]));  // open: dp
  Hex_Digit_Display R3L (.value(R3_q[3:0]));  // open: dp
  Hex_Digit_Display R2L (.value(R2_q[3:0]));  // open: dp
  Hex_Digit_Display R1L (.value(R1_q[3:0]));  // open: dp
  Hex_Digit_Display R0L (.value(R0_q[3:0]));  // open: dp
  Multiplexer #(.select(2), .width(8)) multiplexer_1 (
    .in0(R0_q), .in1(R1_q), .in2(R2_q), .in3(R3_q), .out(RA), .sel(dir_RA));
  Multiplexer #(.select(2), .width(8)) multiplexer_2 (
    .in0(R0_q), .in1(R1_q), .in2(R2_q), .in3(R3_q), .out(RB), .sel(dir_RB));
endmodule
